# Fritzing sketch arduino_rc522 (saved by Fritzing 0.9.3b)
breadboards: 1

parts:
  Componente2 = RFID-RC522-v2
  Composant1 = Arduino Uno (Rev3)
  LED1 = LED - 3mm [color="Green (555nm)" package="3 mm [THT]"]
  LED2 = LED - 3mm [color="Red (633nm)" package="3 mm [THT]"]
  R1 = Resistor [tolerance=±5% resistance=220 package="0603 [SMD]"]
  R2 = Resistor [tolerance=±5% resistance=220 package="0603 [SMD]"]

nets:
  N1: Componente2.SDA, Composant1.D10_PWM/SS
  N2: Componente2.SCK, Composant1.D13/SCK
  N3: Componente2.MOSI, Composant1.D11_PWM/MOSI
  N4: Componente2.MISO, Composant1.D12/MISO
  GND: Componente2.GND, Composant1.GND, LED1.cathode, LED2.cathode
  N5: Componente2.RST, Composant1.D9_PWM
  3.3V: Componente2.3.3V, Composant1.3V3
  N6: Composant1.D6_PWM, R1.Pin_1
  N7: Composant1.D7, R2.Pin_1
  N8: LED1.anode, R2.Pin_0
  N9: LED2.anode, R1.Pin_0

custom parts:
  RFID-RC522-v2: A simple China made RFID-RC522 Reader; do check the pin labels, as this is a MFRC522 based clone.
